# Fritzing sketch Hub Sketch (saved by Fritzing 0.9.4)

parts:
  Part1 = Arduino Mega 2560 (Rev3)
  J1 = Piezo Speaker
  Part2 = Bluetooth HC-05 Macho
  Part3 = NRF24L01
  Part4 = 4x4 Keypad [part_number=101207]
  Display1 = LCD screen 16x2 IIC [part_number=101290]
  R1 = Resistor [tolerance=±5% resistance=1k package=THT]
  R2 = Resistor [tolerance=±5% resistance=2k package=THT]
  C1 = Electrolytic Capacitor [capacitance=10µF voltage=20V package="100 mil [THT, electrolytic]"]

nets:
  N1: Part1.D21/SCL, Part1.SCL, Display1.SCL
  N2: Part1.D20/SDA, Part1.SDA, Display1.SDA
  N3: Part1.D19/RX1, Part2.RXD
  N4: Part1.D18/TX1, R1.Pin_0
  GND: Part1.GND, J1.pin1, Part2.GND, Part3.GND, Display1.GND, R2.Pin_0, C1.-
  N5: Part1.D13_PWM, Part4.1
  N6: Part1.D12_PWM, Part4.2
  N7: Part1.D11_PWM, Part4.3
  N8: Part1.D10_PWM, Part4.4
  N9: Part1.D9_PWM, Part4.5
  N10: Part1.D8_PWM, Part4.6
  3.3V: Part1.3V3, Part3.VCC, C1.+
  N11: Part1.D6_PWM, Part4.8
  N12: Part1.D7_PWM, Part4.7
  5V: Part1.5V, Part2.VCC, Display1.VCC
  N13: Part1.D22, J1.pin2
  N14: Part1.D26, Part3.SCK
  N15: Part1.D48, Part3.CSN
  N16: Part1.D50, Part3.MISO
  N17: Part1.D51, Part3.MOSI
  N18: Part1.D53, Part3.CE
  N19: Part2.TXD, R1.Pin_1, R2.Pin_1

custom parts:
  4x4 Keypad: Matrix membrane keypad 4x4
  LCD screen 16x2 IIC: LCD screen with HD44780 controller enables showing text, symbols, value or anything else that comes from Croduino/Arduino. It is capable of showing 16 symbols in two lines and therefore can be used in many projects that need to send clearly visible and legible output information.. • Color of symbols: White • Backlight: Blue • Dimensions: 80 x 36 x 12 mm • Screen dimensions: 64.5 x 16 mm •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
