# Fritzing sketch RFID Sketch (saved by Fritzing 0.9.4)

parts:
  Part1 = Arduino Uno (Rev3)
  Part2 = RFID-RC522 [part_number=101218]
  Part3 = Bluetooth HC-05 Macho
  Mod1 = KY-011 Two Color LED Module [package="Breakout board"]
  R1 = Resistor [tolerance=±5% resistance=1k package=THT]
  R2 = Resistor [tolerance=±5% resistance=2k package=THT]
  R3 = Resistor [tolerance=±5% resistance=330 package=THT]
  R4 = Resistor [tolerance=±5% resistance=330 package=THT]

nets:
  N1: Part1.D9_PWM, Part2.RST
  N2: Part1.D10_PWM/SS, Part2.SDA
  N3: Part1.D11_PWM/MOSI, Part2.MOSI
  N4: Part1.D12/MISO, Part2.MISO
  N5: Part1.D13/SCK, Part2.SCK
  GND: Part1.GND, Part2.GND, Part3.GND, Mod1.-, R2.Pin_1
  N6: Part1.D2, R3.Pin_0
  N7: Part1.D3_PWM, R4.Pin_0
  N8: Part1.D5_PWM, R1.Pin_0
  N9: Part1.D6_PWM, Part3.RXD
  3.3V: Part1.3V3, Part2.3.3V
  5V: Part1.5V, Part3.VCC
  N10: Part3.TXD, R1.Pin_1, R2.Pin_0
  N11: Mod1.Vin, R4.Pin_1
  N12: Mod1.S, R3.Pin_1

custom parts:
  KY-011 Two Color LED Module: KY-011 Two Color LED Module consist of a common cathode 3mm red/green LED.
