# Fritzing sketch Sensor Sketch 3 (saved by Fritzing 0.9.4)

parts:
  Part1 = Arduino Nano (Rev3.0)
  Part2 = NRF24L01
  PIR1 = PIR sensor

nets:
  GND: Part1.GND, Part2.GND, PIR1.GND
  N1: Part1.D8, PIR1.SIG
  N2: Part1.D9, Part2.CE
  N3: Part1.D10, Part2.CSN
  N4: Part1.D11/MOSI, Part2.MOSI
  N5: Part1.D12/MISO, Part2.MISO
  5V: Part1.5V, Part2.VCC, PIR1.VDD
  N6: Part1.D13/SCK, Part2.SCK
